# Fritzing sketch arduino (saved by Fritzing 0.9.3b)
breadboards: 1

parts:
  Arduino_Nano = Arduino Nano (Rev3.0)
  white = Generic connector 1 Pin [form=male package=THT]
  blue = Generic connector 1 Pin [form=male package=THT]
  RW1 = Resistor [tolerance=±5% resistance=3.3k package=THT]
  RW2 = Resistor [tolerance=±5% resistance=3.3k package=THT]
  grey = Generic connector 1 Pin [form=male package=THT]
  RGREY1 = Resistor [tolerance=±5% resistance=6.6k package=THT]
  RGREY2 = Resistor [tolerance=±5% resistance=3.3k package=THT]
  yellow = Generic connector 1 Pin [form=male package=THT]
  R1 = Resistor [tolerance=±5% resistance=4.7k package=THT]
  R2 = Resistor [tolerance=±5% resistance=4.7k package=THT]
  green = Generic connector 1 Pin [form=male package=THT]
  R1-1 = Resistor [tolerance=±5% resistance=4.7k package=THT]
  R2-1 = Resistor [tolerance=±5% resistance=4.7k package=THT]

nets:
  N1: Arduino_Nano.GND, blue.pin1, RW2.Pin_1, RGREY2.Pin_1, R2.Pin_1, R2-1.Pin_1
  N2: Arduino_Nano.D2, RW1.Pin_1, RW2.Pin_0
  N3: Arduino_Nano.A2, RGREY1.Pin_1, RGREY2.Pin_0
  N4: Arduino_Nano.A1, R1.Pin_1, R2.Pin_0
  N5: Arduino_Nano.A0, R1-1.Pin_1, R2-1.Pin_0
  N6: white.pin1, RW1.Pin_0
  N7: grey.pin1, RGREY1.Pin_0
  N8: yellow.pin1, R1.Pin_0
  N9: green.pin1, R1-1.Pin_0

notes:
  VDO Wind NMEA converter 2020/05/29

custom parts:
  Generic connector 1 Pin: Generic male header
